// Logisim project WaterTankSystem.circ as structural Verilog: 7 circuits, main circuit MainSystem
module SensorEncoder (
  input  S0,
  input  S1,
  input  S2,
  input  S3,
  output L1,
  output L0
);

  wire A1_out, N1_out;

  not N1 (N1_out, S2);
  and A1 (A1_out, S1, N1_out);
  or O1 (L1, S2, S3);
  or O2 (L0, S3, A1_out);
endmodule

module FullComparator (
  input  L1,
  input  L0,
  output FULL
);

  and G1 (FULL, L1, L0);
endmodule

module PumpController (
  input  FULL,
  output PUMP
);

  not N1 (PUMP, FULL);
endmodule

module LevelRegister (
  input  L1,
  input  L0,
  input  CLOCK,
  input  RESET,
  output Q1,
  output Q0
);

  D_Flip_Flop FF1 (.D(L1), .clk(CLOCK), .Q(Q1), .reset(RESET));  // open: Qn, preset
  D_Flip_Flop FF0 (.D(L0), .clk(CLOCK), .Q(Q0), .reset(RESET));  // open: Qn, preset

  // Other names for the same wires on the sheet: CLK = CLOCK; RST = RESET
endmodule

module MainSystem (
  input  S0,
  input  S1,
  input  S2,
  input  S3,
  input  CLOCK,
  input  RESET,
  output Q1,
  output Q0
);

  wire a, A1_out, A3_out, A4_out, A5_out, c, CQ0, CQ0N, CQ1, e, f, FULL, L0, L1, N1_out, N2_out, N4_out,
       N5_out, O3_out, O4_out;

  not N1 (N1_out, S2);
  and A1 (A1_out, S1, N1_out);
  or O1 (L1, S2, S3);
  D_Flip_Flop R1 (.D(L1), .clk(CLOCK), .Q(Q1), .reset(RESET));  // open: Qn, preset
  D_Flip_Flop R0 (.D(L0), .clk(CLOCK), .Q(Q0), .reset(RESET));  // open: Qn, preset
  or O2 (L0, A1_out, S3);
  and A2 (FULL, L1, L0);
  not N3 (e, L0);
  not N4 (N4_out, L1);
  not N2 (N2_out, FULL);
  or O3 (O3_out, CQ1, CQ0);
  or O4 (O4_out, CQ1, CQ0N);
  or O5 (a, e, L1);
  not N5 (N5_out, L1);
  or O6 (c, N4_out, L0);
  and A3 (A3_out, FULL, O3_out);
  and A4 (A4_out, O4_out, FULL);
  and A6 (f, N5_out, e);
  and A5 (A5_out, CQ1, CQ0);
  LED PUMP (.in(N2_out));
  D_Flip_Flop C1 (.D(A3_out), .clk(CLOCK), .Q(CQ1), .reset(RESET));  // open: Qn, preset
  D_Flip_Flop C0 (.D(A4_out), .clk(CLOCK), .Q(CQ0), .Qn(CQ0N), .reset(RESET));  // open: preset
  _7_Segment_Display #(.decimalPoint("false")) u_7_segment_display_1 (
    .g(L1), .f(f), .a(a), .b(1'b1), .e(e), .d(a), .c(c));
  LED ALARM (.in(A5_out));

  // Other names for the same wires on the sheet: CLK = CLOCK; RST = RESET

  // Notes on the sheet:
  //   Water Sensors
  //   Priority Encoder
  //   Level Register
  //   Full Comparator and Pump
  //   7-Segment Decoder
  //   Overflow Counter and Alarm
endmodule

module OverflowCounter (
  input  FULL,
  input  CLOCK,
  input  RESET,
  output Q1,
  output ALARM,
  output Q0
);

  wire A0_out, A1_out, O0_out, O1_out, Q0N;

  or O1 (O1_out, Q1, Q0);
  or O0 (O0_out, Q1, Q0N);
  and A1 (A1_out, FULL, O1_out);
  and A0 (A0_out, FULL, O0_out);
  D_Flip_Flop FF1 (.D(A1_out), .clk(CLOCK), .Q(Q1), .reset(RESET));  // open: Qn, preset
  D_Flip_Flop FF0 (.D(A0_out), .clk(CLOCK), .Q(Q0), .Qn(Q0N), .reset(RESET));  // open: preset
  and A2 (ALARM, Q1, Q0);

  // Other names for the same wires on the sheet: CLK = CLOCK; RST = RESET
endmodule

module SevenSegmentDecoder (
  input  L1,
  input  L0,
  output g,
  output a,
  output d,
  output b,
  output e,
  output c,
  output f
);

  wire nL1;

  not N1 (nL1, L1);
  not N0 (e, L0);
  or Ga (a, L1, e);
  or Gc (c, nL1, L0);
  and Gf (f, nL1, e);

  assign b = 1'b1;
  assign d = a;
  assign g = L1;

  // Other names for the same wires on the sheet: nL0 = e
endmodule
